# Fritzing sketch switch-interface (saved by Fritzing 0.9.6b)
breadboards: 1

parts:
  Mod1 = Raspberry Pi Pico W
  IC1 = Microchip MCP23008 8-bit I/O expander [part_number=MCP23008 package="DIP (Dual Inline) [THT]"]
  IC2 = Microchip MCP23008 8-bit I/O expander [part_number=MCP23008 package="DIP (Dual Inline) [THT]"]
  R1 = Resistor [tolerance=±5% resistance=4.7k power=0.25 package=THT]
  R2 = Resistor [tolerance=±5% resistance=4.7k power=0.25 package=THT]
  S2 = Pushbutton [package="[THT]"]
  LED1 = LED - 5mm [color="Red (633nm)" current=0.030 package="5 mm [THT]"]
  R3 = Resistor [tolerance=±5% resistance=220 power=0.25 package=THT]
  D1 = Diode [package=diode-1n4148]

nets:
  VSS: Mod1.pin_3, Mod1.pin_8, Mod1.pin_13, Mod1.pin_18, Mod1.pin_23, Mod1.pin_28, Mod1.pin_33, Mod1.pin_38, Mod1.pin_42, IC1.A2, IC1.A1, IC1.A0, IC1.VSS, IC2.A2, IC2.A1, IC2.VSS, S2.Pin_1, S2.Pin_2
  N1: Mod1.pin_6, IC1.SDA, IC2.SDA, R2.Pin_1
  N2: Mod1.pin_7, IC1.SCL, IC2.SCL, R1.Pin_1
  N3: Mod1.pin_36, R1.Pin_0, R2.Pin_0
  N4: Mod1.pin_39, D1.C
  VDD: IC1.Reset, IC1.VDD, IC2.A0, IC2.Reset, IC2.VDD, R3.Pin_0, D1.A
  N5: IC1.GP0, LED1.cathode
  N6: S2.Pin_3, S2.Pin_4
  N7: LED1.anode, R3.Pin_1

notes:
  5V power supply

custom parts:
  Raspberry Pi Pico W: Raspberry Pi Pico W. Based around the RP2040 microcontroller the Pico W is a low cost microcontroller device bringing Raspberry Pi quality, cost, and easy of use to the microcontroller space. The areas marked KEEPOUT in pcb silkscreen should not have traces running through them to avoid shorts on a soldered in module!
  Microchip MCP23008 8-bit I/O expander: Provides 8-bit, general purpose, parallel I/O expansion for I2C bus. Datasheet: http://ww1.microchip.com/downloads/en/devicedoc/21919e.pdf
